# Fritzing sketch Thermostat (saved by Fritzing 0.9.3b)
breadboards: 1

parts:
  U1 = RELAY [package=relay-jzc]
  Part1 = Adafruit HUZZAH32 ESP32 Feather [part_number="Adafruit #3405"]
  S1 = Momentary Switch [package=ksa_sealed_tac_switch]
  S2 = Momentary Switch [package=ksa_sealed_tac_switch]
  RHT1 = Humidity and Temperature Sensor RHT03
  R1 = Resistor [tolerance=±5% resistance=10k package=THT]
  Grove1 = Grove OLED 128x96
  V1 = DC Power [voltage=5]  # not connected

nets:
  N1: U1.COIL2, Part1.A1_DAC1
  GND: U1.COIL1, Part1.GND, S1.1, S1.2, S2.1, S2.2, RHT1.GND_2, Grove1.GND
  N2: Part1.SCK, S2.3, S2.4
  VCC: Part1.3.3V, RHT1.Vcc, R1.Pin_0, Grove1.VCC
  N3: Part1.IO12_A11, S1.3, S1.4
  N4: Part1.IO33_A9, RHT1.Data-signal, R1.Pin_1
  N5: Part1.SCL, Grove1.SCL
  N6: Part1.SDA, Grove1.SDA
